# Fritzing sketch GPSTrackerDIY (saved by Fritzing 0.9.4)

parts:
  U2 = NodeMCU V1.0
  GY-NEO6MV3 = SUP500F [package=sup500f]
  VCC1 = Battery

nets:
  N1: U2.GND, GY-NEO6MV3.RX-I
  N2: U2.3V3, GY-NEO6MV3.TX-O, VCC1.+
  N3: U2.RSV#40, GY-NEO6MV3.VCC
  N4: U2.RSV#41, GY-NEO6MV3.GND

notes:
  GND: Black
  VCC: Red
  RX: Yellow
  TX: Green

custom parts:
  NodeMCU V1.0: ESP8266 based NodeMCU
